# Fritzing sketch arduinoled (saved by Fritzing 0.9.3b)
breadboards: 1

parts:
  Part1 = Arduino Uno (Rev3)
  R1 = Resistor [tolerance=±5% resistance=220 package=THT]
  R2 = Resistor [tolerance=±5% resistance=220 package=THT]
  R3 = Resistor [tolerance=±5% resistance=220 package=THT]
  R4 = Resistor [tolerance=±5% resistance=220 package=THT]
  R5 = Resistor [tolerance=±5% resistance=220 package=THT]
  LED1 = LED - 5mm [color="Red (633nm)" package="5 mm [THT]"]
  LED2 = LED - 5mm [color="Green (565nm)" package="5 mm [THT]"]  # not connected
  LED3 = LED - 5mm [color="Blue (470nm)" package="5 mm [THT]"]  # not connected
  LED4 = LED - 5mm [color="Yellow (592nm)" package="5 mm [THT]"]
  LED5 = LED - 5mm [color="White (6500K)" package="5 mm [THT]"]

nets:
  N1: Part1.D8, R1.Pin_1
  N2: Part1.D9_PWM, R2.Pin_1
  N3: Part1.D10_PWM/SS, R3.Pin_1
  N4: Part1.D11_PWM/MOSI, R4.Pin_1
  N5: Part1.D12/MISO, R5.Pin_1
  N6: R1.Pin_0, LED5.anode
  N7: R2.Pin_0, LED4.anode
  N8: R5.Pin_0, LED1.anode
